# Fritzing sketch neopellet-pcbmax31856 (saved by Fritzing 1.0.1rc)
circuit board: 10cm x 7cm
breadboards: 1

parts:
  OLED1 = OLED 128x64 I2C Monochrome Display
  ExtruderMotor = female pin header, 8 pins [form="♀ (female)"]
  RobotIn = female pin header, 3 pins [form="♀ (female)"]
  heatOut = female pin header, 3 pins [form="♀ (female)"]
  temp = KY-040 Rotary encoder [package=THT]
  M1 = DOIT Esp32 DevKit v1 (30 pins long, 11 pins width) [part_number=ESP32S-PIN30]
  fan = KY-040 Rotary encoder [package=THT]
  RE3 = KY-040 Rotary encoder [package=THT]
  fanOut = female pin header, 3 pins [form="♀ (female)"]
  jumper = female pin header, 1 pin [form="♀ (female)"]
  jumper1 = female pin header, 1 pin [form="♀ (female)"]
  jumper2 = female pin header, 1 pin [form="♀ (female)"]
  jumper3 = female pin header, 1 pin [form="♀ (female)"]
  robot1 = female pin header, 4 pins [form="♀ (female)"]
  jumper6 = female alternating pin header, 1 pin [form="♀ (female)"]  # not connected
  jumper5 = rounded female pin header, 1 pin [form="♀ (female rounded)"]  # not connected
  jumper4 = female pin header, 1 pin [form="♀ (female)"]  # not connected
  jumper7 = female pin header, 1 pin [form="♀ (female)"]  # not connected
  Part3 = Adafruit MAX31856 Thermocouple Amp [part_number="Adafruit #3263"]

nets:
  GND: OLED1.GND, ExtruderMotor.pin1, ExtruderMotor.pin2, ExtruderMotor.pin3, RobotIn.pin2, heatOut.pin2, temp.GND, M1.GND, fan.GND, RE3.GND, fanOut.pin2, jumper.pin1, jumper1.pin1, jumper2.pin1, jumper3.pin1, robot1.pin4, Part3.GND
  VCC: OLED1.VDD, RobotIn.pin1, heatOut.pin1, temp.Vcc, M1.VIN, fan.Vcc, RE3.Vcc, fanOut.pin1, robot1.pin3, Part3.VIN
  N1: OLED1.SCK, M1.D22, robot1.pin2
  N2: OLED1.SDA, M1.D21, robot1.pin1
  N3: ExtruderMotor.pin5, M1.D27
  N4: ExtruderMotor.pin6, M1.D26
  N5: ExtruderMotor.pin7, M1.D25
  N6: RobotIn.pin3, M1.D13, Part3.SDI
  N7: heatOut.pin3, M1.D12
  N8: temp.SW, M1.D18
  N9: temp.DT, M1.D19
  N10: temp.CLK, M1.RX0
  N11: M1.D15, fan.SW
  N12: M1.D2, fan.DT
  N13: M1.D4, fan.CLK
  N14: M1.RX2, RE3.SW
  N15: M1.TX2, RE3.DT
  N16: M1.D5, RE3.CLK
  N17: M1.D34, Part3.DRDY
  N18: M1.D35, Part3.SDO
  N19: M1.D32, Part3.SCK
  N20: M1.D33, Part3.!CS
  N21: M1.D14, fanOut.pin3

custom parts:
  KY-040 Rotary encoder: KY-040 Rotary Encoder with switch on breakout borad from AZ Delivery
  DOIT Esp32 DevKit v1 (30 pins long, 11 pins width): The DOIT Esp32 DevKit v1 is one of the development board created by DOIT to evaluate the ESP-WROOM-32 module. It is based on the ESP32 microcontroller that boasts Wifi, Bluetooth, Ethernet and Low Power support all in a single chip. (vanepp) made breadboard work, adjusted pin numbering and labels and reduced size of schematic and cleaned up pcb. This chip is 30pins long (2 x15) and 11 pins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
  Adafruit MAX31856 Thermocouple Amp: Thermocouples are very sensitive, requiring a good amplifier with a cold-compensation reference, as well as calculations to handle any non-linearities. For a long time we've suggested our MAX31855K breakout, which works great but is only for K-type thermocouples. Now we're happy to offer a great new thermocouple amplifier/converter that can handle just about any type of thermocouple, and even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
