# Fritzing sketch signalconverter (saved by Fritzing 0.9.10b)
circuit board: 13.8946cm x 7.94273cm
breadboards: 1

parts:
  M1 = RioRand LM2596
  M4 = RioRand LM2596
  M5 = RioRand LM2596
  M2 = RioRand LM2596
  M3 = RioRand LM2596
  IN = female pin header, 5 pins [form="♀ (female)"]
  out1 = female pin header, 2 pins [form="♀ (female)"]
  out2 = female pin header, 2 pins [form="♀ (female)"]
  out3 = female pin header, 2 pins [form="♀ (female)"]
  out4 = female pin header, 2 pins [form="♀ (female)"]
  out5 = female pin header, 2 pins [form="♀ (female)"]

nets:
  N1: M1.Pin_1, IN.pin5
  N2: M1.Pin_2, M1.Pin_4, out1.pin2
  N3: M1.Pin_3, out1.pin1
  N4: M4.Pin_1, IN.pin4
  N5: M4.Pin_2, M4.Pin_4, out2.pin2
  N6: M4.Pin_3, out2.pin1
  N7: M5.Pin_1, IN.pin3
  N8: M5.Pin_2, M5.Pin_4, out3.pin2
  N9: M5.Pin_3, out3.pin1
  N10: M2.Pin_1, IN.pin2
  N11: M2.Pin_2, M2.Pin_4, out4.pin2
  N12: M2.Pin_3, out4.pin1
  N13: M3.Pin_1, IN.pin1
  N14: M3.Pin_2, M3.Pin_4, out5.pin2
  N15: M3.Pin_3, out5.pin1
